# Fritzing sketch ArduinoMega2Cansat (saved by Fritzing 0.9.0b)
breadboards: 1

parts:
  Part1 = Arduino Mega 2560 (Rev3)
  J2 = female pin header, 10 pins [form="♀ (female)"]
  J1 = female pin header, 10 pins [form="♀ (female)"]
  J3 = female pin header, 10 pins [form="♀ (female)"]
  J4 = female pin header, 10 pins [form="♀ (female)"]
  J5 = female pin header, 10 pins [form="♀ (female)"]
  J6 = female pin header, 10 pins [form="♀ (female)"]

nets:
  N1: Part1.A8, J2.pin9
  N2: Part1.A9, J1.pin9
  N3: Part1.A10, J2.pin8
  N4: Part1.A11, J1.pin8
  N5: Part1.A0, J2.pin7
  N6: Part1.A1, J1.pin7
  N7: Part1.A2, J2.pin6
  N8: Part1.A3, J1.pin6
  N9: Part1.A4, J2.pin5
  N10: Part1.A5, J1.pin5
  N11: Part1.A6, J2.pin4
  N12: Part1.A7, J1.pin4
  N13: Part1.D15/RX3, J5.pin2
  N14: Part1.D14/TX3, J6.pin2
  N15: Part1.D13_PWM, J5.pin3
  N16: Part1.D12_PWM, J6.pin3
  N17: Part1.D11_PWM, J5.pin4
  N18: Part1.D10_PWM, J6.pin4
  N19: Part1.D9_PWM, J5.pin5
  N20: Part1.D8_PWM, J6.pin5
  N21: Part1.5V, J2.pin1, J1.pin10, J3.pin10, J4.pin1, J5.pin10, J6.pin1
  N22: Part1.GND, J2.pin10, J1.pin1, J3.pin1, J4.pin10, J5.pin1, J6.pin10
  N23: Part1.D0_RX0, J6.pin9
  N24: Part1.D1_TX0, J5.pin9
  N25: Part1.D2_PWM, J6.pin8
  N26: Part1.D3_PWM, J5.pin8
  N27: Part1.D4_PWM, J6.pin7
  N28: Part1.D5_PWM, J5.pin7
  N29: Part1.D6_PWM, J6.pin6
  N30: Part1.D7_PWM, J5.pin6
  N31: Part1.D24, J4.pin9
  N32: Part1.D25, J3.pin9
  N33: Part1.D26, J4.pin8
  N34: Part1.D27, J3.pin8
  N35: Part1.D28, J4.pin7
  N36: Part1.D29, J3.pin7
  N37: Part1.D30, J4.pin6
  N38: Part1.D31, J3.pin6
  N39: Part1.D32, J4.pin5
  N40: Part1.D33, J3.pin5
  N41: Part1.D34, J4.pin4
  N42: Part1.D35, J3.pin4
  N43: Part1.D36, J4.pin3
  N44: Part1.D37, J3.pin3
  N45: Part1.D38, J4.pin2
  N46: Part1.D39, J3.pin2
  N47: Part1.D52, J2.pin2
  N48: Part1.D53, J1.pin2
